// Logisim project lab 2 gate diagrams 2.circ as structural Verilog: 1 circuit, main circuit main
module main (
  input  in_1,
  input  in_2,
  input  [7:0] in_3,
  input  [1:0] in_4,
  input  [2:0] in_5,
  input  [7:0] in_6,
  input  in_7,
  input  in_8,
  output [7:0] out_9
);

  wire demultiplexer_1_out0, demultiplexer_1_out1, demultiplexer_1_out2, demultiplexer_1_out3,
       demultiplexer_1_out4, demultiplexer_1_out5, demultiplexer_1_out6, demultiplexer_1_out7,
       demultiplexer_2_out0, demultiplexer_2_out1, demultiplexer_2_out2, demultiplexer_2_out3, undriven;
  wire [7:0] ram_1_data, rom_1_data;

  Demultiplexer #(.select(3), .enable("false")) demultiplexer_1 (
    .out0(demultiplexer_1_out0), .out1(demultiplexer_1_out1), .out2(demultiplexer_1_out2),
    .out3(demultiplexer_1_out3), .out4(demultiplexer_1_out4), .out5(demultiplexer_1_out5),
    .out6(demultiplexer_1_out6), .out7(demultiplexer_1_out7), .in(in_1), .sel(in_5));
  Demultiplexer #(.select(2), .enable("false")) demultiplexer_2 (
    .out0(demultiplexer_2_out0), .out1(demultiplexer_2_out1), .out2(demultiplexer_2_out2),
    .out3(demultiplexer_2_out3), .in(in_2), .sel(in_4));
  RAM ram_1 (.addr(in_3), .data(ram_1_data));  // open: sel, clk, ld, clr
  ROM rom_1 (.addr(in_6), .data(rom_1_data));  // open: sel
  Multiplexer #(.width(8)) multiplexer_1 (.in0(ram_1_data), .in1(rom_1_data), .out(out_9), .sel(in_7), .en(undriven));

  // Notes on the sheet:
  //   contents of rom_1 (hex, n*v repeats v):
  //   0 0 0 3 5
endmodule
