// Logisim project lab2 gate diagrams.circ as structural Verilog: 1 circuit, main circuit main
module main (
  input  in_1,
  input  A,
  input  in_3,
  input  in_4,
  input  B,
  input  C_in,
  input  in_7,
  input  in_8,
  input  in_9,
  input  in_10,
  input  in_11,
  input  in_12,
  output out_13,
  output out_14,
  output out_15,
  output out_16,
  output out_17,
  output out_18,
  output out_19
);

  wire and_2_out, and_3_out, and_4_out, and_5_out, and_6_out, not_2_out, not_3_out;

  or or_1 (out_13, in_1, in_4);
  not xnor_1 (out_15, in_8);  // XNOR_Gate
  not not_1 (out_17, in_9);
  and and_1 (out_19, in_11, in_12);
  not not_2 (not_2_out, in_3);
  not not_3 (not_3_out, in_10);
  and and_2 (and_2_out, not_2_out, in_10);
  and and_3 (and_3_out, in_3, not_3_out);
  or or_2 (out_16, and_2_out, and_3_out);
  xor SUM (out_14, A, B, C_in);
  and and_4 (and_4_out, A, B);
  and and_5 (and_5_out, A, C_in);
  and and_6 (and_6_out, B, C_in);
  or C_out (out_18, and_4_out, and_5_out, and_6_out);
endmodule
